# Fritzing sketch Polargraph (saved by Fritzing 0.9.10b)
breadboards: 1

parts:
  Stepdown_Voltage1 = Polulu Stepdown Voltage [part_number=D24V25F3,D24V25F5]
  C1 = Electrolytic Capacitor [capacitance=100µF voltage=50V package="100 mil [THT, electrolytic]"]
  esp1 = ESP32 DevKitc V4
  M1 = Stepper Motor - Bipolar
  M2 = Stepper Motor - Bipolar
  Pololu_A2 = Pololu A4988 [package=SO16]
  Pololu_A3 = Pololu A4988 [package=SO16]

nets:
  N1: Stepdown_Voltage1.VIn, C1.+, Pololu_A2.VMOT, Pololu_A3.VMOT
  GND: Stepdown_Voltage1.GND, C1.-, esp1.GND, Pololu_A2.GND, Pololu_A3.GND
  VDD: Stepdown_Voltage1.VOut, esp1.5V, Pololu_A2.MS1, Pololu_A2.MS2, Pololu_A2.VDD, Pololu_A3.MS1, Pololu_A3.MS2, Pololu_A3.VDD
  N2: esp1.IO4, Pololu_A3.STEP
  N3: esp1.IO5, Pololu_A3.DIR
  N4: esp1.IO12, Pololu_A2.STEP
  N5: esp1.IO13, Pololu_A2.DIR
  N6: M1.A, Pololu_A2.1A
  N7: M1.C, Pololu_A2.2A
  N8: M1.B, Pololu_A2.1B
  N9: M1.D, Pololu_A2.2B
  N10: M2.A, Pololu_A3.1A
  N11: M2.C, Pololu_A3.2A
  N12: M2.B, Pololu_A3.1B
  N13: M2.D, Pololu_A3.2B
  N14: Pololu_A2.RESET, Pololu_A2.SLEEP
  N15: Pololu_A3.RESET, Pololu_A3.SLEEP

notes:
  +
  -
  12V
  GND
  100µF
  5V

custom parts:
  Polulu Stepdown Voltage: Polulu Stepdown Voltage 3V3 or 5V, 2.5A
  ESP32 DevKitc V4: ESP32-DevKitC board with ESP32-WROOM-32 module. ESP32-DevKitC V4 is a small-sized ESP32-based development board produced by Espressif. Most of the pins on the ESP module are broken out to the pin headers on the board. The pins D0, D1, D2, D3, CMD and CLK are used internally for communication between ESP32 and SPI flash memory. They are grouped on both sides near the USB connector. Avoid using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
